// Logisim project register-file.circ as structural Verilog: 1 circuit, main circuit main
module main (
  input  [7:0] rd,
  input  we,
  input  [2:0] ra,
  input  [2:0] rb,
  input  [2:0] rw,
  input  reset,
  output [7:0] qa,
  output [7:0] qb
);

  wire and_1_out, and_2_out, and_3_out, and_4_out, and_5_out, and_6_out, and_7_out, and_8_out, clk_out,
       decoder_1_out0, decoder_1_out1, decoder_1_out2, decoder_1_out3, decoder_1_out4, decoder_1_out5,
       decoder_1_out6, decoder_1_out7, not_1_out;
  wire [7:0] r0_q, r1_q, r2_q, r3_q, r4_q, r5_q, r6_q, r7_q;

  Decoder #(.select(3), .enable("false")) decoder_1 (
    .out0(decoder_1_out0), .out1(decoder_1_out1), .out2(decoder_1_out2), .out3(decoder_1_out3),
    .out4(decoder_1_out4), .out5(decoder_1_out5), .out6(decoder_1_out6), .out7(decoder_1_out7), .sel(rw));
  Clock clk (.out(clk_out));
  and and_1 (and_1_out, decoder_1_out0, we);
  and and_2 (and_2_out, decoder_1_out1, we);
  and and_3 (and_3_out, decoder_1_out2, we);
  and and_4 (and_4_out, decoder_1_out3, we);
  and and_5 (and_5_out, decoder_1_out4, we);
  and and_6 (and_6_out, decoder_1_out5, we);
  and and_7 (and_7_out, decoder_1_out6, we);
  and and_8 (and_8_out, decoder_1_out7, we);
  not not_1 (not_1_out, reset);
  Register r0 (.D(rd), .en(and_1_out), .Q(r0_q), .clk(clk_out), .clr(not_1_out));
  Register r4 (.D(rd), .en(and_5_out), .Q(r4_q), .clk(clk_out), .clr(not_1_out));
  Register r1 (.D(rd), .en(and_2_out), .Q(r1_q), .clk(clk_out), .clr(not_1_out));
  Register r5 (.D(rd), .en(and_6_out), .Q(r5_q), .clk(clk_out), .clr(not_1_out));
  Register r2 (.D(rd), .en(and_3_out), .Q(r2_q), .clk(clk_out), .clr(not_1_out));
  Register r6 (.D(rd), .en(and_7_out), .Q(r6_q), .clk(clk_out), .clr(not_1_out));
  Register r3 (.D(rd), .en(and_4_out), .Q(r3_q), .clk(clk_out), .clr(not_1_out));
  Register r7 (.D(rd), .en(and_8_out), .Q(r7_q), .clk(clk_out), .clr(not_1_out));
  Multiplexer #(.select(3), .width(8), .enable("false")) multiplexer_1 (
    .in0(r0_q), .in1(r1_q), .in2(r2_q), .in3(r3_q), .in4(r4_q), .in5(r5_q), .in6(r6_q), .in7(r7_q), .out(qa),
    .sel(ra));
  Multiplexer #(.select(3), .width(8), .enable("false")) multiplexer_2 (
    .in0(r0_q), .in1(r1_q), .in2(r2_q), .in3(r3_q), .in4(r4_q), .in5(r5_q), .in6(r6_q), .in7(r7_q), .out(qb),
    .sel(rb));
endmodule
